# Fritzing sketch circuit (saved by Fritzing 1.0.4)
breadboards: 1

parts:
  부품1 = Arduino Leonardo (Rev3b)
  SW_CENTER_R = Pushbutton [package="[THT]"]
  SW_TRACK_3_R = Pushbutton [package="[THT]"]
  SW_TRACK_2_R = Pushbutton [package="[THT]"]
  SW_TRACK_1_R = Pushbutton [package="[THT]"]
  SW_SIDE_R = Pushbutton [package="[THT]"]
  SW_SIDE_L = Pushbutton [package="[THT]"]
  SW_CENTER_R_2 = Pushbutton [package="[THT]"]
  SW_TRACK_3_L = Pushbutton [package="[THT]"]
  SW_TRACK_1_L = Pushbutton [package="[THT]"]
  SW_TRACK_2_L = Pushbutton [package="[THT]"]
  D6 = P1000K [part_number=P1000K]
  D5 = P1000K [part_number=P1000K]
  D7 = P1000K [part_number=P1000K]
  D8 = P1000K [part_number=P1000K]
  D9 = P1000K [part_number=P1000K]
  D4 = P1000K [part_number=P1000K]
  D3 = P1000K [part_number=P1000K]
  D2 = P1000K [part_number=P1000K]
  D1 = P1000K [part_number=P1000K]
  D0 = P1000K [part_number=P1000K]

nets:
  N1: 부품1.D3_PWM/SCL, 부품1.SCL, D4.cathode, D3.cathode, D2.cathode, D1.cathode, D0.cathode
  N2: 부품1.D4/A6, D6.cathode, D5.cathode, D7.cathode, D8.cathode, D9.cathode
  N3: 부품1.D5_PWM, SW_SIDE_R.Pin_3, SW_SIDE_R.Pin_4, SW_SIDE_L.Pin_3, SW_SIDE_L.Pin_4
  N4: 부품1.D6_PWM/A7, SW_TRACK_1_R.Pin_3, SW_TRACK_1_R.Pin_4, SW_TRACK_1_L.Pin_3, SW_TRACK_1_L.Pin_4
  N5: 부품1.D7, SW_TRACK_2_R.Pin_3, SW_TRACK_2_R.Pin_4, SW_TRACK_2_L.Pin_3, SW_TRACK_2_L.Pin_4
  N6: 부품1.D8/A8, SW_TRACK_3_R.Pin_3, SW_TRACK_3_R.Pin_4, SW_TRACK_3_L.Pin_3, SW_TRACK_3_L.Pin_4
  N7: 부품1.D9_PWM/A9, SW_CENTER_R.Pin_3, SW_CENTER_R.Pin_4, SW_CENTER_R_2.Pin_3, SW_CENTER_R_2.Pin_4
  N8: SW_CENTER_R.Pin_1, SW_CENTER_R.Pin_2, D9.anode
  N9: SW_TRACK_3_R.Pin_1, SW_TRACK_3_R.Pin_2, D8.anode
  N10: SW_TRACK_2_R.Pin_1, SW_TRACK_2_R.Pin_2, D7.anode
  N11: SW_TRACK_1_R.Pin_1, SW_TRACK_1_R.Pin_2, D6.anode
  N12: SW_SIDE_R.Pin_1, SW_SIDE_R.Pin_2, D5.anode
  N13: SW_SIDE_L.Pin_1, SW_SIDE_L.Pin_2, D0.anode
  N14: SW_CENTER_R_2.Pin_1, SW_CENTER_R_2.Pin_2, D4.anode
  N15: SW_TRACK_3_L.Pin_1, SW_TRACK_3_L.Pin_2, D3.anode
  N16: SW_TRACK_1_L.Pin_1, SW_TRACK_1_L.Pin_2, D1.anode
  N17: SW_TRACK_2_L.Pin_1, SW_TRACK_2_L.Pin_2, D2.anode

notes:
  LEFT
  RIGHT
